# Fritzing sketch 2 (saved by Fritzing 0.9.3b)

parts:
  Part1 = Arduino Pro Mini v13
  LED1 = LED - 5mm [color="Infrared (940nm)" package="5 mm [THT]"]  # not connected
  LED2 = LED - 5mm [color="Infrared (850nm)" package="5 mm [THT]"]
  J1 = Basic Servo
  R1 = Resistor [tolerance=±5% resistance=100 package=THT]
  R2 = Resistor [tolerance=±5% resistance=100 package=THT]
  Power_plug1 = Power plug
  JP1 = Header 4 [package=screwterminal-3.5mm-4_lock]
  C1 = Ceramic Capacitor [capacitance=100nF package="100 mil [THT, multilayer]"]  # not connected

nets:
  N1: Part1.D0/TX, JP1.4
  N2: Part1.D1/RX, JP1.3
  N3: Part1.VCC, LED2.anode, JP1.2
  GND: Part1.GND, J1.gnd, R1.Pin_1, Power_plug1.GND, JP1.1
  VCC: Part1.RAW, J1.vcc, Power_plug1.VCC
  N4: Part1.D5_PWM, J1.pulse
  N5: Part1.D4, R2.Pin_1
